# Fritzing sketch testPlatformCircuit (saved by Fritzing 0.9.3b)
breadboards: 4

parts:
  Part1 = Arduino Nano (Rev3.0)
  U1 = POT [package=pot_mammoth]
  U2 = POT [package=pot_mammoth]
  U3 = POT [package=pot_mammoth]
  U4 = POT [package=pot_mammoth]
  U5 = POT [package=pot_mammoth]
  U6 = POT [package=pot_mammoth]

nets:
  N1: Part1.GND, U1.E, U2.E, U3.E, U4.E, U5.E, U6.E
  N2: Part1.5V, U1.S, U2.S, U3.S, U4.S, U5.S, U6.S
  N3: Part1.A5, U6.A
  N4: Part1.A4, U5.A
  N5: Part1.A3, U4.A
  N6: Part1.A2, U3.A
  N7: Part1.A1, U2.A
  N8: Part1.A0, U1.A
